# Fritzing sketch DHT11-module (saved by Fritzing 0.9.10b)
breadboards: 1

parts:
  PART1 = Pi Wedge B+
  Raspberry_Pi_1 = Raspberry Pi 3 [part_number=RPI-3-V1.2]  # not connected
  DHT11_1 = DHT11 module

nets:
  N1: PART1.GPIO_26, PART1.G26
  N2: PART1.GPIO_19, PART1.G19
  N3: PART1.GPIO_13, PART1.G13
  N4: PART1.GPIO_6, PART1.G6
  N5: PART1.GPIO_5, PART1.G5
  N6: PART1.ID_SD, PART1.IDSD
  N7: PART1.GPIO_11_(SPI_SCLK), PART1.SCK
  N8: PART1.GPIO_9_(SPI_MISO), PART1.MISO
  N9: PART1.GPIO_10_(SPI_MOSI), PART1.MOSI
  N10: PART1.GPIO_22, PART1.G22
  N11: PART1.GPIO_27, PART1.G27
  N12: PART1.GPIO_17, PART1.G17
  N13: PART1.GPIO_4_(GPCLK0), PART1.G4, DHT11_1.DATA
  N14: PART1.GPIO_3_(I2C1_SCL), PART1.SCL
  N15: PART1.3.3V#19, PART1.3.3V#55
  N16: PART1.GPIO_21, PART1.G21
  N17: PART1.GPIO_20, PART1.G20
  N18: PART1.GPIO_16, PART1.G16
  N19: PART1.GPIO_12, PART1.G12
  N20: PART1.ID_SC, PART1.IDSC
  N21: PART1.GPIO_7_(SPI_CE1), PART1.CE1
  N22: PART1.GPIO_8_(SPI_CE0), PART1.CE0
  N23: PART1.GPIO_25, PART1.G25
  N24: PART1.GPIO_24, PART1.G24
  N25: PART1.GPIO_23, PART1.G23
  N26: PART1.GPIO_18, PART1.G18
  N27: PART1.GPIO_15_(UART_RXD), PART1.RXI
  N28: PART1.5V#54, DHT11_1.VCC
  GND: PART1.GND, DHT11_1.GND

custom parts:
  Pi Wedge B+: This is the Pi Wedge B Plus, a board that connects to the Raspberry Pi B+’s 40-pin GPIO connector, and breaks the pins out to breadboard-friendly arrangement and spacing, and even adds a couple of decoupling capacitors on the power supply lines. The “Wedge” also makes the initial bringup process easier - you can plug an FTDI Basic module into the built-in serial port. Each Pi Wedge comes as an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
  DHT11 module: https://cdn-learn.adafruit.com/downloads/pdf/dht.pdf DHT11 black pcb module reference by:https://github.com/adafruit/Fritzing-Library/blob/master/parts/DHT11%20Humitidy%20and%20Temperature%20Sensor.fzpz
